# Fritzing sketch GY-521 IMU (saved by Fritzing 0.9.3b)
breadboards: 1

parts:
  GY-1 = GY-521 [part_number=GY-521]
  U1 = NodeMCU V1.0

nets:
  3.3V: GY-1.VCC, U1.3V3
  GND: GY-1.GND, GY-1.ADO, U1.GND
  N1: GY-1.SCL, U1.D1
  N2: GY-1.SDA, U1.D2
  5V: U1.Vin

custom parts:
  NodeMCU V1.0: ESP8266 based NodeMCU
